// Logisim project H2.circ as structural Verilog: 2 circuits, main circuit P2
module P2 (
  input  S1,
  input  S0,
  input  In,
  output S1n,
  output S0n,
  output Out
);


  // Notes on the sheet:
  //   PROBLEM 2: IMPLEMENTING A STATE TABLE
  //   INPUT SECTION: Do not change anything here!
  //   You may only change the values of the inputs for testing using the hand tool.
  //   Do not introduce any other input or output pins in the circuit.
  //   To your logic
  //   OUTPUT SECTION: Do not change anything here!
  //   Do not introduce any other input or output pins in the circuit.
  //   From your logic
endmodule

module P3 (
  input  In,
  output Out
);


  // Notes on the sheet:
  //   PROBLEM 3: IMPLEMENTING A STATE MACHINE
  //   INPUT SECTION: Do not change anything here!
  //   You may only change the values of the inputs for testing using the hand tool.
  //   Do not introduce any other input or output pins in the circuit.
  //   To your logic
  //   OUTPUT SECTION: Do not change anything here!
  //   Do not introduce any other input or output pins in the circuit.
  //   From your logic
endmodule
