// Logisim project memory.circ as structural Verilog: 4 circuits, main circuit main
module main (
  input  WE,
  input  A1,
  input  A0,
  input  D3,
  input  D2,
  input  D1,
  input  D0
);

  wire and_1_out, and_2_out, and_3_out, and_4_out, and_5_out, and_6_out, and_7_out, and_8_out, and_9_out,
       and_10_out, and_11_out, and_12_out, and_13_out, and_14_out, and_15_out, and_16_out, and_17_out,
       and_18_out, and_19_out, and_20_out, and_21_out, and_22_out, and_23_out, and_24_out, or_1_out,
       or_2_out, or_3_out, or_4_out, rslatch_1_out, rslatch_2_out, rslatch_3_out, rslatch_4_out,
       rslatch_5_out, rslatch_6_out, rslatch_7_out, rslatch_8_out, rslatch_9_out, rslatch_10_out,
       rslatch_11_out, rslatch_12_out, rslatch_13_out, rslatch_14_out, rslatch_15_out, rslatch_16_out;

  and and_1 (and_1_out, ~A0, ~A1);  // AND_Gate
  and and_2 (and_2_out, A0, ~A1);  // AND_Gate
  and and_3 (and_3_out, ~A0, A1);  // AND_Gate
  and and_4 (and_4_out, A0, A1);
  and and_5 (and_5_out, and_1_out, WE);
  and and_6 (and_6_out, and_2_out, WE);
  and and_7 (and_7_out, and_3_out, WE);
  and and_8 (and_8_out, and_4_out, WE);
  RSLatch rslatch_1 (.D(D3), .WE(and_5_out), .Out(rslatch_1_out));
  and and_9 (and_9_out, rslatch_1_out, and_1_out);
  RSLatch rslatch_2 (.D(D3), .WE(and_6_out), .Out(rslatch_2_out));
  and and_10 (and_10_out, rslatch_2_out, and_2_out);
  RSLatch rslatch_3 (.D(D3), .WE(and_7_out), .Out(rslatch_3_out));
  and and_11 (and_11_out, rslatch_3_out, and_3_out);
  RSLatch rslatch_4 (.D(D3), .WE(and_8_out), .Out(rslatch_4_out));
  and and_12 (and_12_out, rslatch_4_out, and_4_out);
  or or_1 (or_1_out, and_12_out, and_11_out, and_10_out, and_9_out);
  // Probe on or_1_out
  RSLatch rslatch_5 (.D(D2), .WE(and_5_out), .Out(rslatch_5_out));
  and and_13 (and_13_out, rslatch_5_out, and_1_out);
  RSLatch rslatch_6 (.D(D2), .WE(and_6_out), .Out(rslatch_6_out));
  and and_14 (and_14_out, rslatch_6_out, and_2_out);
  RSLatch rslatch_7 (.D(D2), .WE(and_7_out), .Out(rslatch_7_out));
  and and_15 (and_15_out, rslatch_7_out, and_3_out);
  RSLatch rslatch_8 (.D(D2), .WE(and_8_out), .Out(rslatch_8_out));
  and and_16 (and_16_out, rslatch_8_out, and_4_out);
  or or_2 (or_2_out, and_16_out, and_15_out, and_14_out, and_13_out);
  // Probe on or_2_out
  RSLatch rslatch_9 (.D(D1), .WE(and_5_out), .Out(rslatch_9_out));
  RSLatch rslatch_10 (.D(D1), .WE(and_6_out), .Out(rslatch_10_out));
  RSLatch rslatch_11 (.D(D1), .WE(and_7_out), .Out(rslatch_11_out));
  RSLatch rslatch_12 (.D(D1), .WE(and_8_out), .Out(rslatch_12_out));
  and and_17 (and_17_out, rslatch_9_out, and_1_out);
  and and_18 (and_18_out, rslatch_10_out, and_2_out);
  and and_19 (and_19_out, rslatch_11_out, and_3_out);
  and and_20 (and_20_out, rslatch_12_out, and_4_out);
  or or_3 (or_3_out, and_20_out, and_19_out, and_18_out, and_17_out);
  // Probe on or_3_out
  RSLatch rslatch_13 (.D(D0), .WE(and_5_out), .Out(rslatch_13_out));
  RSLatch rslatch_14 (.D(D0), .WE(and_6_out), .Out(rslatch_14_out));
  RSLatch rslatch_15 (.D(D0), .WE(and_7_out), .Out(rslatch_15_out));
  RSLatch rslatch_16 (.D(D0), .WE(and_8_out), .Out(rslatch_16_out));
  and and_21 (and_21_out, rslatch_13_out, and_1_out);
  and and_22 (and_22_out, rslatch_14_out, and_2_out);
  and and_23 (and_23_out, rslatch_15_out, and_3_out);
  and and_24 (and_24_out, rslatch_16_out, and_4_out);
  or or_4 (or_4_out, and_24_out, and_23_out, and_22_out, and_21_out);
  // Probe on or_4_out
endmodule

module RSLatch (
  input  D,
  input  WE,
  output Out
);

  wire nand_1_out, nand_2_out, nand_4_out;

  nand nand_1 (nand_1_out, D, WE);
  nand nand_2 (nand_2_out, WE, ~D);  // NAND_Gate
  nand nand_3 (Out, nand_1_out, nand_4_out);
  nand nand_4 (nand_4_out, Out, nand_2_out);
endmodule

module flipflop (
  input  in_1,
  output out_2,
  output Out
);

  wire clock_1_out, nand_1_out, nand_2_out, nand_4_out, nand_5_out, nand_6_out, nand_8_out, not_1_out,
       not_2_out;

  Clock clock_1 (.out(clock_1_out));
  nand nand_1 (nand_1_out, not_1_out, clock_1_out);
  nand nand_2 (nand_2_out, clock_1_out, ~not_1_out);  // NAND_Gate
  nand nand_3 (out_2, nand_1_out, nand_4_out);
  nand nand_4 (nand_4_out, out_2, nand_2_out);
  not not_1 (not_1_out, Out);
  not not_2 (not_2_out, clock_1_out);
  nand nand_5 (nand_5_out, out_2, not_2_out);
  nand nand_6 (nand_6_out, not_2_out, ~out_2);  // NAND_Gate
  nand nand_7 (Out, nand_5_out, nand_8_out);
  nand nand_8 (nand_8_out, Out, nand_6_out);
endmodule

module RSexample (
  input  in_1,
  input  WE,
  output Out
);

  wire nand_1_out, nand_2_out, nand_4_out, not_1_out;

  not not_1 (not_1_out, Out);
  nand nand_1 (nand_1_out, not_1_out, WE);
  nand nand_2 (nand_2_out, WE, ~not_1_out);  // NAND_Gate
  nand nand_3 (Out, nand_1_out, nand_4_out);
  nand nand_4 (nand_4_out, Out, nand_2_out);
endmodule
